# Fritzing sketch RealTimeClockDS1307 (saved by Fritzing 0.5.2b)
breadboards: 1

parts:
  Arduino1 = Arduino
  U1 = Mystery Part - 5 pins
  LED1 = Red LED - 5mm [package="5 mm [THT]"]
  R1 = Resistor [resistance=220 package=THT]

nets:
  N1: Arduino1.GND, U1.connector1
  N2: Arduino1.+5V, U1.connector0, R1.Pin_1
  N3: Arduino1.A4, U1.connector4
  N4: Arduino1.A5, U1.connector3
  N5: U1.connector2, LED1.cathode
  N6: LED1.anode, R1.Pin_0

notes:
  The Sparkfun DS1307 module is actually square and red. Just follow the labels on the pins.
  LED/Resistor are optional for showing the square wave.
